# Fritzing sketch RadioMarellino (saved by Fritzing 1.0.3b)
circuit board: 8.78869cm x 8.13703cm
breadboards: 1

parts:
  M1 = ESP32-S2-DevKitC-1 [part_number=ESP32-S2-DevKitC-1]
  RIGHT = Adafruit MAX98357A I2S 3W Class D Amplifier [part_number="Adafruit #3006"]
  A1 = DD4012SA [package=THT]
  A2 = DD4012SA [package=THT]
  RE1 = KY-040 Rotary encoder [package="Breakout board"]
  J1 = screw terminal, 2 pins
  R3 = Resistor [tolerance=±5% power=0.25W resistance=220 package=THT]
  R4 = Resistor [tolerance=±5% power=0.25W resistance=220 package=THT]
  R5 = Resistor [tolerance=±5% power=0.25W resistance=220 package=THT]
  R6 = Resistor [tolerance=±5% power=0.25W resistance=220 package=THT]
  LEFT = Adafruit MAX98357A I2S 3W Class D Amplifier [part_number="Adafruit #3006"]
  RE2 = KY-040 Rotary encoder [package="Breakout board"]

nets:
  VCC: M1.pin_1, M1.pin_2, RE1.Vcc, RE2.Vcc
  N1: M1.pin_18, RIGHT.DIN, R5.Pin_0, LEFT.DIN
  N2: M1.pin_19, RIGHT.BCLK, R6.Pin_0, LEFT.BCLK
  N3: M1.pin_20, RIGHT.LRCLK, LEFT.LRCLK
  N4: M1.pin_21, A2.pin3
  GND: M1.pin_22, M1.pin_23, M1.pin_24, M1.pin_44, RIGHT.GND, A1.pin2, A2.pin2, RE1.GND, J1.pin1, LEFT.GND, RE2.GND
  N5: M1.pin_38, RE1.CLK
  N6: M1.pin_42, RE1.DT
  N7: M1.pin_43, RE1.SW
  VIN: RIGHT.VIN, A1.pin3, R3.Pin_1, R4.Pin_1, R5.Pin_1, R6.Pin_1, LEFT.VIN
  N8: RIGHT.SD_MODE, R3.Pin_0
  N9: A1.pin1, A2.pin1, J1.pin2
  N10: R4.Pin_0, LEFT.SD_MODE

custom parts:
  ESP32-S2-DevKitC-1: ESP32-S2-DevKitC-1 is an entry-level development board based on ESP32-S2-SOLO (on-board PCB antenna). It is based on the ESP32 microcontroller that boasts Wifi, Bluetooth, Ethernet and Low Power support all in a single chip. (vanepp) Feb 2022: converted to ESP32-S2-DevKitC-1. This module is 44pins long (2x22) and 11 pins width.
  Adafruit MAX98357A I2S 3W Class D Amplifier: Listen to this good news - we now have an all in one digital audio amp breakout board that works incredibly well with the Raspberry Pi! If you're looking for an easy and low cost way to get you digital sound files bumpin' then the MAX08357 I2S Amp Breakout is for you. It takes standard I2S digital audio input and, not only decodes it into analog, but also amplifies it directly into a speaker.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
  DD4012SA: DD4012SA 1A DC 5V 6V 9V 12V 24V to 3.3V 5V DC-DC Step-Down Buck Converter Regulator Module Board.
  KY-040 Rotary encoder: KY-040 Rotary Encoder with switch on breakout borad from AZ Delivery
